# Fritzing sketch MultiplexerYuda (saved by Fritzing 0.9.3b)

parts:
  Part1 = Analog Digital MUX Breakout
  Part2 = Arduino Mega 2560 (Rev3)
  Part3 = Analog Digital MUX Breakout
  Part4 = Analog Digital MUX Breakout
  Part5 = Analog Digital MUX Breakout

nets:
  GND: Part1.GND, Part2.GND, Part3.GND, Part4.GND, Part5.GND
  VCC: Part1.VCC, Part2.5V, Part3.VCC, Part4.VCC, Part5.VCC
  N1: Part1.S0, Part2.D5_PWM, Part3.S0, Part4.S0, Part5.S0
  N2: Part1.S1, Part2.D4_PWM, Part3.S1, Part4.S1, Part5.S1
  N3: Part1.S2, Part2.D3_PWM, Part3.S2, Part4.S2, Part5.S2
  N4: Part1.S3, Part2.D2_PWM, Part3.S3, Part4.S3, Part5.S3
  N5: Part1.SIG, Part2.D8_PWM
  N6: Part2.D9_PWM, Part4.SIG
  N7: Part2.D6_PWM, Part5.SIG
  N8: Part2.D7_PWM, Part3.SIG
